# Fritzing sketch hitachi_display_i2c (saved by Fritzing 0.7.11b)
stripboards: 1

parts:
  U2 = atmega168 [package=dip]
  Y1 = Resonator [frequency="16 Mhz" package=THT]
  LCD1 = LCD screen
  R1 = Trimmer Potentiometer [maximum_resistance=10kΩ package=THT]
  J2 = male pin header, 6 pins [form="♂ (male)"]
  J3 = male pin header, 3 pins [form="♂ (male)"]
  J4 = male pin header, 3 pins [form="♂ (male)"]  # not connected
  LED1 = LED - 5mm [color="Red (633nm)" package="5 mm [THT]"]

nets:
  N1: U2.RESET, J3.pin1
  N2: U2.D0_(RX), J2.pin6
  N3: U2.D1_(TX), J2.pin5
  N4: U2.D2, LCD1.DB7
  N5: U2.D3_(PWM), LCD1.DB6
  N6: U2.D4, LCD1.DB5
  VCC: U2.VCC, LCD1.VDD, LCD1.DB1, LCD1.LED+, R1.leg1
  GND: U2.GND#7, Y1.GND, LCD1.VSS, LCD1.R/W, LCD1.DB3, LCD1.LED-, R1.leg2, LED1.cathode
  N7: U2.XLAT1, Y1.pin_1
  N8: U2.XLAT2, Y1.0
  N9: U2.D5_(PWM), LCD1.DB0, LCD1.DB4
  N10: U2.D7, LCD1.E
  N11: U2.D8, LCD1.RS
  N12: U2.D9_(PWM), LED1.anode
  N13: U2.D12, J3.pin3
  N14: U2.D13, J3.pin2
  N15: U2.AVCC, J2.pin4
  N16: U2.GND#21, J2.pin3
  N17: U2.A4, J2.pin1
  N18: U2.A5, J2.pin2
  N19: LCD1.V0, LCD1.DB2, R1.wiper
