# Fritzing sketch nokia_display_and_nfc_i2c (saved by Fritzing 0.8.7b)
stripboards: 1

parts:
  J1 = female pin header, 8 pins [form="♀ (female)"]
  Y1 = Resonator [frequency="16 Mhz" package=THT]  # not connected
  J2 = male pin header, 4 pins [form="♂ (male)"]
  J3 = female pin header, 8 pins [form="♀ (female)"]
  LED1 = RGB LED (com. anode, rbg) [package="5 mm [THT]"]
  U2 = atmega328 [package=dip]

nets:
  N1: J1.pin1, J1.pin2, J1.pin3, J1.pin4, J1.pin5, J1.pin6, J1.pin7, J1.pin8, J2.pin1, J2.pin2, J2.pin3, J2.pin4, J3.pin1, J3.pin2, J3.pin3, J3.pin4, J3.pin5, J3.pin6, J3.pin7, J3.pin8, U2.D2, U2.D7, U2.D8, U2.D9_(PWM), U2.D11_(PWM), U2.D13, U2.AVCC, U2.GND#21, U2.A0, U2.A1, U2.A2, U2.A3, U2.A4
  N2: LED1.red_cathode, U2.D3_(PWM)
  N3: LED1.common_anode, U2.GND#7
  N4: LED1.blue_cathode, U2.D5_(PWM)
  N5: LED1.green_cathode, U2.D6_(PWM)

notes:
  Nokia Display
